# Fritzing sketch arduino_demo (saved by Fritzing 0.9.0b)
breadboards: 1

parts:
  Part1 = Arduino Uno (Rev3)
  LED1 = RGB LED (com. cathode, rgb) [package="5 mm [THT]"]
  U1 = POT [package=pot_mammoth]
  R4 = Resistor [tolerance=±5% resistance=1k package=THT]
  R5 = Resistor [tolerance=±5% resistance=1k package=THT]
  R6 = Resistor [tolerance=±5% resistance=1k package=THT]
  J1 = Basic Servo

nets:
  N1: Part1.A0, U1.A
  N2: Part1.D9_PWM, J1.pulse
  N3: Part1.D3_PWM, LED1.red_anode, R6.Pin_0, R6.Pin_1
  N4: Part1.D5_PWM, LED1.green_anode, R4.Pin_0, R4.Pin_1
  N5: Part1.D6_PWM, LED1.blue_anode, R5.Pin_0, R5.Pin_1
  5V: Part1.5V, U1.S, J1.vcc
  GND: Part1.GND, LED1.common_cathode, U1.E, J1.gnd
